# Fritzing sketch wiring (saved by Fritzing 0.9.3b)

parts:
  Bauteil1 = Arduino Pro Mini (3.3V)
  Config-Taster = Momentary Switch [package=ksa_sealed_tac_switch]
  STATUS_LED = LED - 3mm [color="Green (560nm)" package="3 mm [THT]"]
  R1 = Resistor [tolerance=±5% resistance=330 package=THT]
  Antenne_~8_3cm = CC1101 [part_number=CC1101]
  DFRobot_DFPlayer_Mini1 = DFRobot DFPlayer Mini [part_number=DFR0299]
  Bauteil2 = ws2812b [package="smd 2812b"]
  Bauteil3 = ws2812b [package="smd 2812b"]
  Bauteil4 = ws2812b [package="smd 2812b"]
  R2+R3 = Resistor [tolerance=±5% resistance=1k package=THT]
  R4 = Resistor [tolerance=±5% resistance=1k package=THT]
  SPKR1 = Loudspeaker
  PNP = PNP-Transistor [package="TO92 [THT]"]
  3_3V_Reed-Relais = RELAY [package=OJ]
  R5 = Resistor [tolerance=±5% resistance=1k package=THT]
  D1 = Rectifier Diode [part_number=1N4001 package="Melf DO-213 AB [SMD]"]

nets:
  VDD: Bauteil1.RAW, Bauteil2.VDD, Bauteil3.VDD, Bauteil4.VDD
  VSS: Bauteil1.GND, Config-Taster.4, STATUS_LED.cathode, Antenne_~8_3cm.2, DFRobot_DFPlayer_Mini1.GND-1, DFRobot_DFPlayer_Mini1.GND-2, Bauteil2.VSS, Bauteil3.VSS, Bauteil4.VSS, 3_3V_Reed-Relais.COIL1, D1.anode
  VCC: Bauteil1.VCC, Antenne_~8_3cm.1, DFRobot_DFPlayer_Mini1.VCC, PNP.E
  N1: Bauteil1.SCK, Antenne_~8_3cm.4
  N2: Bauteil1.MISO, Antenne_~8_3cm.5
  N3: Bauteil1.MOSI, Antenne_~8_3cm.3
  N4: Bauteil1.D10, Antenne_~8_3cm.8
  N5: Bauteil1.D9, R2+R3.Pin_1
  N6: Bauteil1.D8, R4.Pin_1
  N7: Bauteil1.D7, Bauteil2.DIN
  N8: Bauteil1.D6, Config-Taster.3
  N9: Bauteil1.D5, DFRobot_DFPlayer_Mini1.BUSY, R5.Pin_1
  N10: Bauteil1.D4, R1.Pin_0
  N11: Bauteil1.D2, Antenne_~8_3cm.7
  N12: STATUS_LED.anode, R1.Pin_1
  N13: DFRobot_DFPlayer_Mini1.RX, R2+R3.Pin_0
  N14: DFRobot_DFPlayer_Mini1.TX, R4.Pin_0
  N15: DFRobot_DFPlayer_Mini1.SPK_1, SPKR1.pin2
  N16: DFRobot_DFPlayer_Mini1.SPK_2, 3_3V_Reed-Relais.NO
  N17: Bauteil2.DOUT, Bauteil3.DIN
  N18: Bauteil3.DOUT, Bauteil4.DIN
  N19: SPKR1.pin1, 3_3V_Reed-Relais.MAIN
  N20: PNP.B, R5.Pin_0
  N21: PNP.C, 3_3V_Reed-Relais.COIL2, D1.cathode
